# Fritzing sketch circuit_diagram (saved by Fritzing 0.9.10b)
breadboards: 1

parts:
  LCD1 = LCD screen
  Part1 = Arduino Uno (Rev3) - ICSP
  WeMos_D1_Mini_Relay_Shield_V1 = WeMos D1 Mini Relay Shield V2
  WeMos_D1_Mini_Relay_Shield_V2 = WeMos D1 Mini Relay Shield V2
  Part2 = Soil Moisture Sensor
  R2 = Resistor [tolerance=±5% resistance=3700 package="0603 [SMD]"]
  R1 = Resistor [tolerance=±5% power=0.25 resistance=220 package=THT]
  Part3 = Soil Moisture Sensor
  Power_plug1 = Power plug
  M1 = DC Motor [voltage_(max)=6V voltage_(min)=3V]

nets:
  GND: LCD1.VSS, LCD1.R/W, LCD1.LED-, Part1.GND, WeMos_D1_Mini_Relay_Shield_V1.G, Part2.GND, Part3.GND
  VDD: LCD1.VDD, Part1.5V, WeMos_D1_Mini_Relay_Shield_V2.NO, R2.Pin_0, R1.Pin_0
  N1: LCD1.V0, R2.Pin_1
  N2: LCD1.RS, Part1.D12/MISO
  N3: LCD1.E, Part1.D10_PWM/SS
  N4: LCD1.DB4, Part1.D5_PWM
  N5: LCD1.DB5, Part1.D4
  N6: LCD1.DB6, Part1.D3_PWM
  N7: LCD1.DB7, Part1.D2
  N8: LCD1.LED+, R1.Pin_1
  N9: Part1.A0, Part2.SIG
  N10: Part1.A1, Part3.SIG
  N11: Part1.D8, WeMos_D1_Mini_Relay_Shield_V2.RST
  N12: Part1.D7, WeMos_D1_Mini_Relay_Shield_V1.RST
  3V3: Part1.3V3, WeMos_D1_Mini_Relay_Shield_V2.3V3
  N13: WeMos_D1_Mini_Relay_Shield_V1.COM, M1.pin_2
  N14: WeMos_D1_Mini_Relay_Shield_V1.NO, Power_plug1.VCC
  VCC: WeMos_D1_Mini_Relay_Shield_V2.COM, Part2.VCC, Part3.VCC
  N15: Power_plug1.GND, M1.pin_1
